# Fritzing sketch Sequencia (saved by Fritzing 1.0.6)
breadboards: 1

parts:
  Componente1 = Arduino Uno (Rev3)
  LED1 = smd LED [color="Red (633nm)" package="0603 [SMD]"]
  LED2 = smd LED [color="Red (633nm)" package="0603 [SMD]"]
  LED3 = smd LED [color="Red (633nm)" package="0603 [SMD]"]
  LED4 = smd LED [color="Red (633nm)" package="0603 [SMD]"]
  LED5 = smd LED [color="Red (633nm)" package="0603 [SMD]"]

nets:
  N1: Componente1.GND, LED1.cathode, LED2.cathode, LED3.cathode, LED4.cathode, LED5.cathode
  N2: Componente1.D1/TX, LED5.anode
  N3: Componente1.D2, LED4.anode
  N4: Componente1.D3_PWM, LED3.anode
  N5: Componente1.D4, LED2.anode
  N6: Componente1.D5_PWM, LED1.anode
